// Logisim project logic_gates.circ as structural Verilog: 1 circuit, main circuit main
module main (
  input  A,
  input  B,
  input  C,
  input  D,
  input  E,
  input  F,
  input  G,
  input  H,
  input  I,
  input  X,
  input  Y,
  input  in_12,
  input  in_13,
  output out_14,
  output out_15,
  output out_16,
  output out_17,
  output out_18,
  output out_19,
  output out_20
);

  wire AND1_out, AND2_out, and_2_out, and_3_out, and_4_out, and_5_out, and_6_out, not_1_out, not_2_out,
       not_3_out, not_4_out, not_5_out, not_6_out, not_7_out, not_8_out, not_12_out, or_1_out;

  not not_1 (not_1_out, F);
  not not_2 (not_2_out, G);
  not not_3 (not_3_out, H);
  not not_4 (not_4_out, I);
  not not_5 (not_5_out, Y);
  not not_6 (not_6_out, X);
  not not_7 (not_7_out, in_13);
  not not_8 (not_8_out, in_12);
  not not_9 (out_14, A);
  and and_1 (out_15, B, C);
  and and_2 (and_2_out, D, E);
  and and_3 (and_3_out, not_1_out, not_2_out);
  and and_4 (and_4_out, not_3_out, not_4_out);
  and AND1 (AND1_out, X, not_5_out);
  and AND2 (AND2_out, not_6_out, Y);
  and and_5 (and_5_out, in_12, not_7_out);
  and and_6 (and_6_out, not_8_out, in_13);
  not not_10 (out_16, and_2_out);
  not not_11 (out_17, and_3_out);
  not not_12 (not_12_out, and_4_out);
  not not_13 (out_18, not_12_out);
  or OR1 (out_19, AND1_out, AND2_out);
  or or_1 (or_1_out, and_5_out, and_6_out);
  not not_14 (out_20, or_1_out);

  // Notes on the sheet:
  //   NOT
  //   AND
  //   NAND
  //   OR
  //   NOR
  //   XOR
  //   XNOR
endmodule
